# Fritzing sketch blink_02 (saved by Fritzing 0.9.0b)
breadboards: 1

parts:
  Componente1 = Arduino Leonardo (Rev3b)
  LED1 = smd LED [color="Red (633nm)" package="0805 [SMD]"]
  R1 = Resistor [tolerance=±5% resistance=330 package=THT]

nets:
  N1: Componente1.D13_PWM, R1.Pin_0
  N2: Componente1.GND, LED1.cathode
  N3: LED1.anode, R1.Pin_1
