# Fritzing sketch blink_01 (saved by Fritzing 0.9.0b)

parts:
  Componente1 = Arduino Leonardo (Rev3b)
  LED1 = smd LED [color="Red (633nm)" package="0603 [SMD]"]

nets:
  N1: Componente1.D13_PWM, LED1.anode
  N2: Componente1.GND, LED1.cathode
