# Fritzing sketch projeto_04_comunicacao_bluetooth (saved by Fritzing 0.9.0b)

parts:
  JY-MCU = JY-MCU
  Componente1 = Arduino Leonardo (Rev3b)
  LED1 = smd LED [color="Red (633nm)" package="0603 [SMD]"]

nets:
  N1: JY-MCU.TX, Componente1.D0/RX
  VCC: JY-MCU.VCC, Componente1.5V
  N2: JY-MCU.RX, Componente1.D1/TX
  GND: JY-MCU.GND, Componente1.GND, LED1.cathode
  N3: Componente1.D13_PWM, LED1.anode

custom parts:
  JY-MCU: Description: The Bluetooth Mate is very similar to our BlueSMiRF modem, but it is designed specifically to be used with our Arduino Pros and LilyPad Arduinos. These modems work as a serial (RX/TX) pipe, and are a great wireless replacement for serial cables. Any serial stream from 9600 to 115200bps can be passed seamlessly from your computer to your target. Bluetooth Mate has the same pin out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
