# Fritzing sketch projeto_06_servo (saved by Fritzing 0.9.0b)

parts:
  Componente1 = Arduino Leonardo (Rev3b)
  J1 = Basic Servo

nets:
  5V: Componente1.5V, J1.vcc
  GND: Componente1.GND, J1.gnd
  N1: Componente1.D9_PWM/A9, J1.pulse
