# Fritzing sketch projeto_08_botao_led (saved by Fritzing 0.9.0b)
breadboards: 1

parts:
  Componente1 = Arduino Leonardo (Rev3b)
  LED2 = smd LED [color="Red (633nm)" package="0603 [SMD]"]
  R2 = Resistor [tolerance=±5% resistance=330 package=THT]
  S1 = Pushbutton [package="[THT]"]
  R3 = Resistor [tolerance=±5% resistance=10k package=THT]

nets:
  N1: Componente1.D6_PWM/A7, R2.Pin_1
  N2: Componente1.D7, S1.Pin_1, S1.Pin_2, R3.Pin_0
  N3: Componente1.5V, R3.Pin_1
  N4: Componente1.GND, LED2.cathode, S1.Pin_3, S1.Pin_4
  N5: LED2.anode, R2.Pin_0
