# Fritzing sketch projeto_10_buzzer_piano (saved by Fritzing 0.9.0b)
breadboards: 1

parts:
  Componente1 = Arduino Leonardo (Rev3b)
  LED2 = smd LED [color="Red (633nm)" package="0603 [SMD]"]
  R2 = Resistor [tolerance=±5% resistance=330 package=THT]
  S1 = Pushbutton [package="[THT]"]
  R3 = Resistor [tolerance=±5% resistance=10k package=THT]
  S2 = Pushbutton [package="[THT]"]
  LED3 = smd LED [color="Yellow (585nm)" package="0603 [SMD]"]
  R4 = Resistor [tolerance=±5% resistance=10k package=THT]
  R5 = Resistor [tolerance=±5% resistance=330 package=THT]
  S3 = Pushbutton [package="[THT]"]
  LED4 = smd LED [color="Green (555nm)" package="0603 [SMD]"]
  R6 = Resistor [tolerance=±5% resistance=10k package=THT]
  R7 = Resistor [tolerance=±5% resistance=330 package=THT]
  J1 = Piezo Speaker

nets:
  N1: Componente1.D1/TX, J1.pin2
  N2: Componente1.D2/SDA, R7.Pin_1
  N3: Componente1.D3_PWM/SCL, S3.Pin_1, S3.Pin_2, R6.Pin_0
  N4: Componente1.D4/A6, R5.Pin_1
  N5: Componente1.D5_PWM, S2.Pin_1, S2.Pin_2, R4.Pin_0
  N6: Componente1.D6_PWM/A7, R2.Pin_1
  N7: Componente1.D7, S1.Pin_1, S1.Pin_2, R3.Pin_0
  N8: Componente1.5V, R3.Pin_1, R6.Pin_1
  N9: Componente1.GND, LED2.cathode, S1.Pin_3, S1.Pin_4, LED3.cathode, S3.Pin_3, S3.Pin_4, LED4.cathode, J1.pin1
  N10: LED2.anode, R2.Pin_0
  N11: S2.Pin_3, S2.Pin_4
  N12: LED3.anode, R5.Pin_0
  N13: LED4.anode, R7.Pin_0
