# Fritzing sketch projeto_11_potenciometro (saved by Fritzing 0.8.7b)
breadboards: 1

parts:
  Componente1 = Arduino Leonardo (Rev3b)
  U1 = POT [package=pot_alpha_rv16af-20]

nets:
  N1: Componente1.5V, U1.E
  N2: Componente1.GND, U1.A
  N3: Componente1.A0, U1.S
