# Fritzing sketch projeto_13_potenciometro_led_pwm (saved by Fritzing 0.9.0b)
breadboards: 1

parts:
  Componente1 = Arduino Leonardo (Rev3b)
  LED1 = smd LED [color="Red (633nm)" package="0603 [SMD]"]
  R1 = Resistor [tolerance=±5% resistance=330 package=THT]
  U1 = POT [package=pot_alpha_rv16af-20]

nets:
  N1: Componente1.D3_PWM/SCL, R1.Pin_1
  N2: Componente1.5V, U1.E
  N3: Componente1.GND, LED1.cathode, U1.A
  N4: Componente1.A0, U1.S
  N5: LED1.anode, R1.Pin_0
