# Fritzing sketch projeto_14_lcd (saved by Fritzing 0.9.0b)
breadboards: 1

parts:
  LCD1 = LCD screen
  Componente1 = Arduino Leonardo (Rev3b)
  U1 = POT [package=pot_alpha_rv16af-20]

nets:
  VSS: LCD1.VSS, LCD1.R/W, LCD1.LED-, Componente1.GND, U1.A
  VDD: LCD1.VDD, LCD1.LED+, Componente1.5V, U1.E
  N1: LCD1.V0, U1.S
  N2: LCD1.RS, Componente1.D12/A11
  N3: LCD1.E, Componente1.D11_PWM
  N4: LCD1.DB4, Componente1.D5_PWM
  N5: LCD1.DB5, Componente1.D4/A6
  N6: LCD1.DB6, Componente1.D3_PWM/SCL
  N7: LCD1.DB7, Componente1.D2/SDA
