# Fritzing sketch projeto_15_lcd_led_botao (saved by Fritzing 0.8.7b)
breadboards: 1

parts:
  LCD1 = LCD screen
  Componente1 = Arduino Leonardo (Rev3b)
  U1 = POT [package=pot_alpha_rv16af-20]
  LED2 = smd LED [color="Red (633nm)" package="0603 [SMD]"]
  R2 = Resistor [tolerance=±5% resistance=330 package=THT]
  S1 = Pushbutton [package="[THT]"]
  R3 = Resistor [tolerance=±5% resistance=10k package=THT]

nets:
  VSS: LCD1.VSS, LCD1.R/W, LCD1.LED-, Componente1.GND, U1.A, LED2.cathode, S1.Pin_3, S1.Pin_4
  VDD: LCD1.VDD, LCD1.LED+, Componente1.5V, U1.E, R3.Pin_1
  N1: LCD1.V0, U1.S
  N2: LCD1.RS, Componente1.D12/A11
  N3: LCD1.E, Componente1.D11_PWM
  N4: LCD1.DB4, Componente1.D5_PWM
  N5: LCD1.DB5, Componente1.D4/A6
  N6: LCD1.DB6, Componente1.D3_PWM/SCL
  N7: LCD1.DB7, Componente1.D2/SDA
  N8: Componente1.D0/RX, R2.Pin_1
  N9: Componente1.D1/TX, S1.Pin_1, S1.Pin_2, R3.Pin_0
  N10: LED2.anode, R2.Pin_0
