# Fritzing sketch projeto_16_ldr (saved by Fritzing 0.9.0b)
breadboards: 1

parts:
  Componente1 = Arduino Leonardo (Rev3b)
  R2 = Photocell (LDR) [package=THT]
  R3 = Resistor [tolerance=±5% resistance=10k package=THT]

nets:
  N1: Componente1.5V, R2.pin_1
  N2: Componente1.GND, R3.Pin_0
  N3: Componente1.A0, R2.pin_0, R3.Pin_1
