# Fritzing sketch projeto_17_ldr_led (saved by Fritzing 0.9.0b)
breadboards: 1

parts:
  Componente1 = Arduino Leonardo (Rev3b)
  R2 = Photocell (LDR) [package=THT]
  R3 = Resistor [tolerance=±5% resistance=10k package=THT]
  LED1 = LED - 5mm [color="Red (633nm)" package="5 mm [THT]"]
  R4 = Resistor [tolerance=±5% resistance=330 package=THT]

nets:
  N1: Componente1.D2/SDA, R4.Pin_1
  N2: Componente1.5V, R2.pin_1
  N3: Componente1.GND, R3.Pin_0, LED1.cathode
  N4: Componente1.A0, R2.pin_0, R3.Pin_1
  N5: LED1.anode, R4.Pin_0
