# Fritzing sketch projeto_18_ntc (saved by Fritzing 0.9.0b)
breadboards: 1

parts:
  Componente1 = Arduino Leonardo (Rev3b)
  R3 = Resistor [tolerance=±5% resistance=10k package=THT]
  R5 = Temperature Sensor (Thermistor) [thermistor_type=NTC package=THT]

nets:
  N1: Componente1.5V, R5.pin_1
  N2: Componente1.GND, R3.Pin_0
  N3: Componente1.A0, R3.Pin_1, R5.pin_0
