# Fritzing sketch projeto_19_termometro (saved by Fritzing 0.9.0b)
breadboards: 1

parts:
  Componente1 = Arduino Leonardo (Rev3b)
  R3 = Resistor [tolerance=±5% resistance=10k package=THT]
  R5 = Temperature Sensor (Thermistor) [thermistor_type=NTC package=THT]
  LED1 = LED - 5mm [color="Red (633nm)" package="5 mm [THT]"]
  LED2 = LED - 5mm [color="Red (633nm)" package="5 mm [THT]"]
  LED3 = LED - 5mm [color="Yellow (585nm)" package="5 mm [THT]"]
  LED4 = LED - 5mm [color="Yellow (585nm)" package="5 mm [THT]"]
  LED5 = LED - 5mm [color="Green (555nm)" package="5 mm [THT]"]
  LED6 = LED - 5mm [color="Green (555nm)" package="5 mm [THT]"]
  R6 = Resistor [tolerance=±5% resistance=330 package=THT]
  R7 = Resistor [tolerance=±5% resistance=330 package=THT]
  R8 = Resistor [tolerance=±5% resistance=330 package=THT]
  R9 = Resistor [tolerance=±5% resistance=330 package=THT]
  R10 = Resistor [tolerance=±5% resistance=330 package=THT]
  R11 = Resistor [tolerance=±5% resistance=330 package=THT]
  J1 = Piezo Speaker

nets:
  N1: Componente1.D6_PWM/A7, J1.pin2
  N2: Componente1.5V, R5.pin_1
  N3: Componente1.GND, R3.Pin_0, LED1.cathode, LED2.cathode, LED3.cathode, LED4.cathode, LED5.cathode, LED6.cathode, J1.pin1
  N4: Componente1.A0, R3.Pin_1, R5.pin_0
  N5: Componente1.D8/A8, R6.Pin_1
  N6: Componente1.D9_PWM/A9, R7.Pin_1
  N7: Componente1.D10_PWM/A10, R8.Pin_1
  N8: Componente1.D11_PWM, R9.Pin_1
  N9: Componente1.D12/A11, R10.Pin_1
  N10: Componente1.D13_PWM, R11.Pin_1
  N11: LED1.anode, R11.Pin_0
  N12: LED2.anode, R10.Pin_0
  N13: LED3.anode, R9.Pin_0
  N14: LED4.anode, R8.Pin_0
  N15: LED5.anode, R7.Pin_0
  N16: LED6.anode, R6.Pin_0
